# Fritzing sketch adxl_wiring (saved by Fritzing 0.9.9b)

parts:
  Mod1 = seeeduino-xiao
  Part1 = Adafruit ADXL345 [part_number="Adafruit #1231"]
  Part2 = Adafruit QT Py RP2040 [part_number="Adafruit #4900"]
  Part3 = Adafruit ADXL345 [part_number="Adafruit #1231"]
  Part4 = Adafruit ADXL345 [part_number="Adafruit #1231"]
  Raspberry_Pi_1 = Raspberry Pi 3 [part_number=RPI-3-V1.2]

nets:
  N1: Mod1.D7, Part1.CS
  N2: Mod1.D8, Part1.SCL
  N3: Mod1.D9, Part1.SDO/ADDR
  N4: Mod1.D10, Part1.SDA/SDIO
  3V3: Mod1.3V3, Part1.3.3V
  GND: Mod1.GND, Part1.GND
  N5: Part2.TX, Part3.SDO/ADDR
  N6: Part2.RX, Part3.CS
  N7: Part2.SCK, Part3.SCL
  N8: Part2.MOSI, Part3.SDA/SDIO
  +3V3: Part2.+3V3, Part3.3.3V
  GND_2: Part2.GND, Part3.GND
  3.3V: Part4.3.3V, Raspberry_Pi_1.3V3
  GND_3: Part4.GND, Raspberry_Pi_1.GND
  N9: Part4.CS, Raspberry_Pi_1.GPIO8
  N10: Part4.SDO/ADDR, Raspberry_Pi_1.GPIO9
  N11: Part4.SDA/SDIO, Raspberry_Pi_1.GPIO10
  N12: Part4.SCL, Raspberry_Pi_1.GPIO11

custom parts:
  seeeduino-xiao: Seeeduino XIAO processor board.
  Adafruit ADXL345: Filling out our accelerometer offerings, we now have the really lovely digital ADXL345 from Analog Devices, a triple-axis accelerometer with digital I2C and SPI interface breakout. We added an on-board 3.3V regulator and logic-level shifting circuitry, making it a perfect choice for interfacing with any 3V or 5V microcontroller such as the Arduino. The sensor has three axes of measurements, X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
  Adafruit QT Py RP2040: Description What a cutie pie! Or is it... a QT Py? This diminutive dev board comes with one of our new favorite chip, the RP2040. It's been made famous in the new Raspberry Pi Pico and our Feather RP2040 and ItsyBitsy RP2040, but what if we wanted something really smol? A new chip means a new QT Py, and the Raspberry Pi RP2040 is no exception. When we saw this chip we thought "this chip is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
